# Fritzing sketch s3smsf (saved by Fritzing 0.9.5d)
breadboards: 2

parts:
  GSM_SIM_GPSR_SMS_SIM900_SIM1 = SIM800L [package=THT]
  Power_5v_2A = Power plug
  C1_4700mF_16v = Electrolytic Capacitor [capacitance=470µF package="100 mil [THT, electrolytic]"]
  OLED_I2C1 = OLED 128x64 I2C Monochrome Display
  U1 = ESP32-38PinWide [part_number=ESP32-38PinWide]

nets:
  5V: GSM_SIM_GPSR_SMS_SIM900_SIM1.5V, Power_5v_2A.VCC, C1_4700mF_16v.+, U1.VIN
  N1: GSM_SIM_GPSR_SMS_SIM900_SIM1.GND#1, Power_5v_2A.GND, C1_4700mF_16v.-, U1.GPIO11
  N2: GSM_SIM_GPSR_SMS_SIM900_SIM1.SIM_TXD, U1.GPIO27
  N3: GSM_SIM_GPSR_SMS_SIM900_SIM1.SIM_RXD, U1.GPIO25
  N4: OLED_I2C1.SDA, U1.GPIO21
  N5: OLED_I2C1.SCK, U1.GPIO22

custom parts:
  ESP32-38PinWide: Generic 38-Pin ESP32 with wide format (only access to one side of pins on a breadboard) based on Stephen Lilley's HiLetgo ESP-WROOM-32 ESP32 ESP-32S Development Board.
